// Logisim project backup.circ as structural Verilog: 1 circuit, main circuit principal
module principal (
  input  v0,
  input  a3,
  input  a2,
  input  a1,
  input  a0,
  input  b3,
  input  b2,
  input  b1,
  input  b0
);

  wire and_1_out, and_2_out, and_3_out, and_4_out, and_5_out, and_6_out, and_7_out, and_8_out, and_9_out,
       and_10_out, and_11_out, and_12_out, and_13_out, and_14_out, and_15_out, and_16_out, and_17_out,
       and_18_out, and_19_out, and_20_out, and_21_out, and_22_out, and_23_out, and_24_out, and_25_out,
       and_26_out, and_27_out, and_28_out, and_29_out, and_30_out, and_31_out, and_32_out, and_33_out,
       and_34_out, and_35_out, and_36_out, and_37_out, and_38_out, and_39_out, and_40_out, and_41_out,
       and_42_out, and_43_out, and_44_out, and_45_out, and_46_out, and_47_out, not_1_out, not_2_out,
       not_3_out, not_4_out, not_5_out, not_6_out, not_7_out, not_8_out, not_9_out, not_10_out, not_11_out,
       not_12_out, not_13_out, not_14_out, not_15_out, not_16_out, not_17_out, not_18_out, not_19_out,
       not_20_out, not_21_out, not_22_out, not_23_out, not_24_out, not_25_out, not_26_out, not_27_out,
       not_28_out, not_29_out, not_30_out, not_31_out, not_32_out, not_33_out, not_34_out, not_35_out,
       not_36_out, not_37_out, not_38_out, not_39_out, not_40_out, not_41_out, not_42_out, not_43_out,
       or_1_out, or_2_out, or_3_out, or_4_out, or_5_out, or_6_out, or_7_out, or_8_out, or_9_out, or_10_out,
       or_11_out, xor_1_out, xor_2_out, xor_3_out, xor_4_out, xor_5_out, xor_6_out, xor_7_out, xor_8_out;

  or or_1 (or_1_out, and_1_out, and_2_out, and_3_out, and_4_out, and_5_out, and_6_out);
  or or_2 (or_2_out, and_7_out, and_8_out, and_9_out, and_10_out, and_11_out);
  or or_3 (or_3_out, and_12_out, and_13_out, and_14_out, and_15_out, and_16_out);
  or or_4 (or_4_out, and_17_out, and_18_out, and_19_out, and_20_out, and_21_out);
  or or_5 (or_5_out, and_22_out, and_23_out, and_24_out, and_25_out, and_26_out);
  or or_6 (or_6_out, and_27_out, and_28_out, and_29_out, and_30_out);
  or or_7 (or_7_out, and_31_out, and_32_out, and_33_out, and_34_out, and_35_out);
  and and_1 (and_1_out, not_1_out, xor_8_out, not_2_out);
  and and_2 (and_2_out, xor_2_out, xor_6_out, not_3_out);
  and and_3 (and_3_out, xor_4_out, not_4_out);
  and and_4 (and_4_out, xor_4_out, xor_6_out);
  and and_5 (and_5_out, not_5_out, xor_8_out);
  and and_6 (and_6_out, not_6_out, not_7_out);
  and and_7 (and_7_out, not_8_out, xor_6_out, not_9_out);
  and and_8 (and_8_out, xor_6_out, not_10_out);
  and and_9 (and_9_out, xor_8_out, not_11_out);
  and and_10 (and_10_out, xor_8_out, xor_4_out);
  and and_11 (and_11_out, not_12_out, not_13_out);
  and and_12 (and_12_out, not_14_out, not_15_out, not_16_out);
  and and_13 (and_13_out, xor_4_out, not_17_out, xor_2_out);
  and and_14 (and_14_out, xor_8_out, not_18_out, xor_2_out);
  and and_15 (and_15_out, not_19_out, not_20_out);
  and and_16 (and_16_out, not_42_out, not_43_out);
  and and_17 (and_17_out, not_21_out, xor_4_out);
  and and_18 (and_18_out, xor_8_out, not_22_out);
  and and_19 (and_19_out, xor_4_out, not_23_out);
  and and_20 (and_20_out, xor_2_out, xor_8_out);
  and and_21 (and_21_out, not_24_out, xor_6_out, not_25_out);
  and and_22 (and_22_out, not_26_out, xor_8_out);
  and and_23 (and_23_out, xor_6_out, not_27_out, xor_2_out);
  and and_24 (and_24_out, not_28_out, not_29_out, not_30_out);
  and and_25 (and_25_out, xor_6_out, xor_4_out, not_31_out);
  and and_26 (and_26_out, xor_2_out, xor_4_out, not_32_out);
  and and_27 (and_27_out, xor_8_out, xor_4_out);
  and and_28 (and_28_out, xor_8_out, xor_6_out);
  and and_29 (and_29_out, not_33_out, xor_4_out);
  and and_30 (and_30_out, not_34_out, not_35_out);
  and and_31 (and_31_out, not_36_out, xor_8_out);
  and and_32 (and_32_out, not_37_out, xor_2_out);
  and and_33 (and_33_out, not_38_out, not_39_out);
  and and_34 (and_34_out, xor_6_out, not_40_out);
  and and_35 (and_35_out, xor_2_out, not_41_out);
  _7_Segment_Display u_7_segment_display_1 (
    .g(or_4_out), .f(or_2_out), .a(or_1_out), .b(or_3_out), .e(or_6_out), .d(or_5_out), .c(or_7_out));  // open: dp
  not not_1 (not_1_out, xor_4_out);
  not not_2 (not_2_out, xor_6_out);
  not not_3 (not_3_out, xor_8_out);
  not not_4 (not_4_out, xor_8_out);
  not not_5 (not_5_out, xor_2_out);
  not not_6 (not_6_out, xor_2_out);
  not not_7 (not_7_out, xor_6_out);
  not not_8 (not_8_out, xor_8_out);
  not not_9 (not_9_out, xor_4_out);
  not not_10 (not_10_out, xor_2_out);
  not not_11 (not_11_out, xor_6_out);
  not not_12 (not_12_out, xor_4_out);
  not not_13 (not_13_out, xor_2_out);
  not not_14 (not_14_out, xor_8_out);
  not not_15 (not_15_out, xor_4_out);
  not not_16 (not_16_out, xor_2_out);
  not not_17 (not_17_out, xor_8_out);
  not not_18 (not_18_out, xor_4_out);
  not not_19 (not_19_out, xor_2_out);
  not not_20 (not_20_out, xor_6_out);
  not not_21 (not_21_out, xor_2_out);
  not not_22 (not_22_out, xor_6_out);
  not not_23 (not_23_out, xor_6_out);
  not not_24 (not_24_out, xor_4_out);
  not not_25 (not_25_out, xor_8_out);
  not not_26 (not_26_out, xor_4_out);
  not not_27 (not_27_out, xor_4_out);
  not not_28 (not_28_out, xor_8_out);
  not not_29 (not_29_out, xor_6_out);
  not not_30 (not_30_out, xor_2_out);
  not not_31 (not_31_out, xor_2_out);
  not not_32 (not_32_out, xor_6_out);
  not not_33 (not_33_out, xor_2_out);
  not not_34 (not_34_out, xor_6_out);
  not not_35 (not_35_out, xor_2_out);
  not not_36 (not_36_out, xor_6_out);
  not not_37 (not_37_out, xor_8_out);
  not not_38 (not_38_out, xor_8_out);
  not not_39 (not_39_out, xor_4_out);
  not not_40 (not_40_out, xor_8_out);
  not not_41 (not_41_out, xor_4_out);
  LED led_1 (.in(or_11_out));
  not not_42 (not_42_out, xor_6_out);
  not not_43 (not_43_out, xor_8_out);
  xor xor_1 (xor_1_out, b0, v0);
  and and_36 (and_36_out, v0, b0);
  and and_37 (and_37_out, b0, a0);
  and and_38 (and_38_out, v0, a0);
  xor xor_2 (xor_2_out, xor_1_out, a0);
  or or_8 (or_8_out, and_36_out, and_37_out, and_38_out);
  xor xor_3 (xor_3_out, or_8_out, b1);
  and and_39 (and_39_out, or_8_out, b1);
  and and_40 (and_40_out, or_8_out, a1);
  and and_41 (and_41_out, b1, a1);
  xor xor_4 (xor_4_out, xor_3_out, a1);
  or or_9 (or_9_out, and_39_out, and_40_out, and_41_out);
  xor xor_5 (xor_5_out, or_9_out, b2);
  and and_42 (and_42_out, or_9_out, a2);
  and and_43 (and_43_out, or_9_out, b2);
  and and_44 (and_44_out, a2, b2);
  xor xor_6 (xor_6_out, xor_5_out, a2);
  or or_10 (or_10_out, and_42_out, and_43_out, and_44_out);
  xor xor_7 (xor_7_out, or_10_out, b3);
  and and_45 (and_45_out, or_10_out, a3);
  and and_46 (and_46_out, or_10_out, b3);
  and and_47 (and_47_out, a3, b3);
  xor xor_8 (xor_8_out, xor_7_out, a3);
  or or_11 (or_11_out, and_45_out, and_46_out, and_47_out);

  // Notes on the sheet:
  //   c
  //   ce
  //   cd
  //   m
  //   b
  //   be
  //   bd
  //   overflow
  //   N0
  //   V1
  //   N1
  //   V2
  //   N2
  //   V3
  //   N4
  //   V4 - loop
endmodule
