// Logisim project displaybackup.circ as structural Verilog: 1 circuit, main circuit main
module main (
  input  a3,
  input  a2,
  input  a1,
  input  a0,
  input  b3,
  input  b2,
  input  b1,
  input  b0
);

  wire and_1_out, and_2_out, and_3_out, and_4_out, and_5_out, and_6_out, and_7_out, and_8_out, and_9_out,
       and_10_out, and_11_out, and_12_out, and_13_out, and_14_out, and_15_out, and_16_out, and_17_out,
       and_18_out, and_19_out, and_20_out, and_21_out, and_22_out, and_23_out, and_24_out, and_25_out,
       and_26_out, and_27_out, and_28_out, and_29_out, and_30_out, and_31_out, and_32_out, and_33_out,
       and_34_out, and_35_out, and_36_out, and_37_out, and_38_out, and_39_out, and_40_out, and_41_out,
       and_42_out, and_43_out, and_44_out, and_45_out, and_46_out, and_47_out, and_48_out, b_out, bd_out,
       be_out, c_out, cd_out, ce_out, m_out, not_1_out, not_2_out, not_3_out, not_4_out, or_1_out, or_2_out,
       or_3_out, or_4_out, xor_1_out, xor_2_out, xor_3_out, xor_4_out;

  not not_1 (not_1_out, xor_4_out);
  not not_2 (not_2_out, xor_3_out);
  not not_3 (not_3_out, xor_1_out);
  not not_4 (not_4_out, xor_2_out);
  and and_1 (and_1_out, not_4_out, not_2_out, xor_4_out);
  and and_2 (and_2_out, xor_1_out, xor_3_out, not_1_out);
  and and_3 (and_3_out, xor_2_out, not_1_out);
  and and_4 (and_4_out, xor_2_out, xor_3_out);
  and and_5 (and_5_out, not_3_out, xor_4_out);
  and and_6 (and_6_out, not_3_out, not_2_out);
  and and_7 (and_7_out, not_1_out, xor_3_out, not_4_out);
  and and_8 (and_8_out, xor_4_out, not_2_out);
  and and_9 (and_9_out, xor_4_out, xor_2_out);
  and and_10 (and_10_out, not_4_out, not_3_out);
  and and_11 (and_11_out, xor_3_out, not_3_out);
  and and_12 (and_12_out, not_1_out, not_4_out, not_3_out);
  and and_13 (and_13_out, not_1_out, xor_2_out, xor_1_out);
  and and_14 (and_14_out, xor_4_out, not_4_out, xor_1_out);
  and and_15 (and_15_out, not_2_out, not_3_out);
  and and_16 (and_16_out, not_2_out, not_1_out);
  and and_17 (and_17_out, not_2_out, not_4_out);
  and and_18 (and_18_out, xor_3_out, not_4_out, not_1_out);
  and and_19 (and_19_out, xor_1_out, xor_4_out);
  and and_20 (and_20_out, xor_2_out, not_2_out);
  and and_21 (and_21_out, not_2_out, xor_4_out);
  and and_22 (and_22_out, not_3_out, xor_2_out);
  and and_23 (and_23_out, xor_1_out, xor_2_out, not_2_out);
  and and_24 (and_24_out, xor_2_out, xor_3_out, not_3_out);
  and and_25 (and_25_out, not_3_out, not_2_out, not_1_out);
  and and_26 (and_26_out, xor_1_out, not_4_out, xor_3_out);
  and and_27 (and_27_out, not_4_out, xor_4_out);
  and and_28 (and_28_out, xor_4_out, xor_2_out);
  and and_29 (and_29_out, xor_4_out, xor_3_out);
  and and_30 (and_30_out, xor_2_out, not_3_out);
  and and_31 (and_31_out, not_2_out, not_3_out);
  and and_32 (and_32_out, xor_4_out, not_2_out);
  and and_33 (and_33_out, not_1_out, xor_1_out);
  and and_34 (and_34_out, not_1_out, not_4_out);
  and and_35 (and_35_out, not_1_out, xor_3_out);
  and and_36 (and_36_out, not_4_out, xor_1_out);
  or c (c_out, and_1_out, and_2_out, and_3_out, and_4_out, and_5_out, and_6_out);
  or ce (ce_out, and_7_out, and_8_out, and_9_out, and_10_out, and_11_out);
  or cd (cd_out, and_14_out, and_12_out, and_13_out, and_15_out, and_16_out, and_17_out);
  or m (m_out, and_18_out, and_19_out, and_20_out, and_21_out, and_22_out);
  or b (b_out, and_23_out, and_24_out, and_25_out, and_26_out, and_27_out);
  or be (be_out, and_28_out, and_29_out, and_30_out, and_31_out);
  or bd (bd_out, and_32_out, and_33_out, and_34_out, and_35_out, and_36_out);
  _7_Segment_Display u_7_segment_display_1 (
    .g(m_out), .f(ce_out), .a(c_out), .b(cd_out), .e(be_out), .d(b_out), .c(bd_out));  // open: dp
  LED led_1 (.in(or_4_out));
  xor xor_1 (xor_1_out, 1'b0, a0, b0);
  and and_37 (and_37_out, 1'b0, b0);
  and and_38 (and_38_out, 1'b0, a0);
  and and_39 (and_39_out, b0, a0);
  or or_1 (or_1_out, and_37_out, and_38_out, and_39_out);
  xor xor_2 (xor_2_out, or_1_out, a1, b1);
  and and_40 (and_40_out, or_1_out, b1);
  and and_41 (and_41_out, a1, or_1_out);
  and and_42 (and_42_out, b1, a1);
  or or_2 (or_2_out, and_40_out, and_41_out, and_42_out);
  xor xor_3 (xor_3_out, or_2_out, a2, b2);
  and and_43 (and_43_out, or_2_out, b2);
  and and_44 (and_44_out, a2, or_2_out);
  and and_45 (and_45_out, b2, a2);
  or or_3 (or_3_out, and_43_out, and_44_out, and_45_out);
  xor xor_4 (xor_4_out, or_3_out, a3, b3);
  and and_46 (and_46_out, or_3_out, b3);
  and and_47 (and_47_out, or_3_out, a3);
  and and_48 (and_48_out, b3, a3);
  or or_4 (or_4_out, and_46_out, and_47_out, and_48_out);

  // Notes on the sheet:
  //   Overflow
endmodule
