// Logisim project trabalho02.circ as structural Verilog: 3 circuits, main circuit main
module main (
);

  wire button_1_out, button_2_out, button_3_out, button_4_out, button_5_out, clock_1_out, d_ff_1_q, d_ff_2_q,
       d_ff_3_q, d_ff_4_q, d_ff_5_q, d_ff_6_q, d_ff_7_q, d_ff_8_q, d_ff_9_q, d_ff_10_q, d_ff_11_q, d_ff_12_q,
       d_ff_13_q, n1transicao_1_d0, n1transicao_1_d1, n1transicao_1_d2, n2transicao_1_agua,
       n2transicao_1_devolve, n2transicao_1_refri, n2transicao_1_troco_0_5, n2transicao_1_troco_1_00;

  Button button_1 (.out(button_1_out));
  Button button_2 (.out(button_2_out));
  Button button_3 (.out(button_3_out));
  Button button_4 (.out(button_4_out));
  Button button_5 (.out(button_5_out));
  Clock clock_1 (.out(clock_1_out));
  D_Flip_Flop d_ff_1 (.clk(clock_1_out), .D(button_1_out), .Q(d_ff_1_q), .preset(button_1_out));  // open: Qn, en, reset
  D_Flip_Flop d_ff_2 (.clk(clock_1_out), .D(button_2_out), .Q(d_ff_2_q), .preset(button_2_out));  // open: Qn, en, reset
  D_Flip_Flop d_ff_3 (.clk(clock_1_out), .D(button_3_out), .Q(d_ff_3_q), .preset(button_3_out));  // open: Qn, en, reset
  D_Flip_Flop d_ff_4 (.clk(clock_1_out), .D(button_4_out), .Q(d_ff_4_q), .preset(button_4_out));  // open: Qn, en, reset
  D_Flip_Flop d_ff_5 (.clk(clock_1_out), .D(button_5_out), .Q(d_ff_5_q), .preset(button_5_out));  // open: Qn, en, reset
  _1transicao u_1transicao_1 (
    .A(d_ff_6_q), .B(d_ff_7_q), .C(d_ff_8_q), .D(d_ff_1_q), .E(d_ff_2_q), .F(d_ff_3_q), .G(d_ff_4_q),
    .H(d_ff_5_q), .D0(n1transicao_1_d0), .D1(n1transicao_1_d1), .D2(n1transicao_1_d2));
  D_Flip_Flop d_ff_6 (.clk(clock_1_out), .D(n1transicao_1_d2), .Q(d_ff_6_q));  // open: Qn, preset, en, reset
  D_Flip_Flop d_ff_7 (.clk(clock_1_out), .D(n1transicao_1_d1), .Q(d_ff_7_q));  // open: Qn, preset, en, reset
  D_Flip_Flop d_ff_8 (.clk(clock_1_out), .D(n1transicao_1_d0), .Q(d_ff_8_q));  // open: Qn, preset, en, reset
  _2transicao u_2transicao_1 (
    .A(d_ff_6_q), .B(d_ff_7_q), .C(d_ff_8_q), .D(d_ff_1_q), .E(d_ff_2_q), .F(d_ff_3_q), .G(d_ff_4_q),
    .H(d_ff_5_q), .Agua(n2transicao_1_agua), .Refri(n2transicao_1_refri), .Devolve(n2transicao_1_devolve),
    .Troco_0_5(n2transicao_1_troco_0_5), .Troco_1_00(n2transicao_1_troco_1_00));
  D_Flip_Flop d_ff_9 (
    .clk(clock_1_out), .D(n2transicao_1_agua), .Q(d_ff_9_q), .preset(n2transicao_1_agua));  // open: Qn, en, reset
  D_Flip_Flop d_ff_10 (
    .clk(clock_1_out), .D(n2transicao_1_refri), .Q(d_ff_10_q), .preset(n2transicao_1_refri));  // open: Qn, en, reset
  D_Flip_Flop d_ff_11 (
    .clk(clock_1_out), .D(n2transicao_1_devolve), .Q(d_ff_11_q), .preset(n2transicao_1_devolve));  // open: Qn, en, reset
  D_Flip_Flop d_ff_12 (
    .clk(clock_1_out), .D(n2transicao_1_troco_0_5), .Q(d_ff_12_q), .preset(n2transicao_1_troco_0_5));  // open: Qn, en, reset
  D_Flip_Flop d_ff_13 (
    .clk(clock_1_out), .D(n2transicao_1_troco_1_00), .Q(d_ff_13_q), .preset(n2transicao_1_troco_1_00));  // open: Qn, en, reset
  LED led_1 (.in(d_ff_9_q));
  LED led_2 (.in(d_ff_10_q));
  LED led_3 (.in(d_ff_11_q));
  LED led_4 (.in(d_ff_12_q));
  LED led_5 (.in(d_ff_13_q));

  // Notes on the sheet:
  //   0,50 centavos
  //   1,00 real
  //   Agua
  //   Refri
  //   Cancela
  //   Agua
  //   Refri
  //   Devolve
  //   Troco 0,50
  //   Troco 1,00
endmodule

module _1transicao (
  input  A,
  input  B,
  input  C,
  input  D,
  input  E,
  input  F,
  input  G,
  input  H,
  output D0,
  output D1,
  output D2
);

  wire and_1_out, and_2_out, and_3_out, and_4_out, and_5_out, and_6_out, and_7_out, and_8_out, and_9_out,
       and_10_out, and_11_out, and_12_out, and_13_out, and_14_out, and_15_out, not_1_out, not_2_out,
       not_3_out, not_4_out, not_5_out, not_6_out, not_7_out, not_8_out;

  not not_1 (not_1_out, A);
  not not_2 (not_2_out, C);
  not not_3 (not_3_out, B);
  not not_4 (not_4_out, E);
  not not_5 (not_5_out, D);
  not not_6 (not_6_out, F);
  not not_7 (not_7_out, G);
  not not_8 (not_8_out, H);
  and and_1 (and_1_out, not_1_out, C, not_5_out, not_4_out, not_6_out, not_8_out);
  and and_2 (and_2_out, not_1_out, C, not_5_out, not_6_out, not_7_out, not_8_out);
  and and_3 (and_3_out, not_3_out, C, not_5_out, not_6_out, not_7_out, not_8_out);
  and and_4 (and_4_out, not_1_out, not_2_out, D, not_4_out, not_6_out, not_7_out, not_8_out);
  and and_5 (and_5_out, not_1_out, not_3_out, C, not_5_out, not_4_out, not_7_out, not_8_out);
  and and_6 (and_6_out, A, not_3_out, D, not_4_out, not_6_out, not_7_out, not_8_out);
  and and_7 (and_7_out, not_1_out, B, not_5_out, not_4_out, not_6_out, not_8_out);
  and and_8 (and_8_out, not_1_out, not_3_out, not_5_out, E, not_6_out, not_7_out, not_8_out);
  and and_9 (and_9_out, not_1_out, B, not_2_out, not_5_out, not_4_out, not_7_out, not_8_out);
  and and_10 (and_10_out, not_1_out, B, not_2_out, not_4_out, not_6_out, not_7_out, not_8_out);
  and and_11 (and_11_out, not_1_out, not_3_out, C, D, not_4_out, not_6_out, not_7_out, not_8_out);
  and and_12 (and_12_out, A, not_3_out, not_5_out, not_6_out, not_7_out, not_8_out);
  and and_13 (and_13_out, A, not_3_out, not_4_out, not_6_out, not_7_out, not_8_out);
  and and_14 (and_14_out, not_1_out, B, not_5_out, E, not_6_out, not_7_out, not_8_out);
  and and_15 (and_15_out, not_1_out, B, C, D, not_4_out, not_6_out, not_7_out, not_8_out);
  or or_1 (D1, and_7_out, and_8_out, and_9_out, and_10_out, and_11_out);
  or or_2 (D2, and_12_out, and_13_out, and_14_out, and_15_out);
  or or_3 (D0, and_1_out, and_2_out, and_3_out, and_4_out, and_5_out, and_6_out);

  // Notes on the sheet:
  //   A
  //   A
  //   C
  //   B
  //   C
  //   D
  //   B
  //   E
  //   D
  //   E
  //   F
  //   F
  //   G
  //   G
  //   H
  //   H
endmodule

module _2transicao (
  input  A,
  input  B,
  input  C,
  input  D,
  input  E,
  input  F,
  input  G,
  input  H,
  output Agua,
  output Refri,
  output Devolve,
  output Troco_0_5,
  output Troco_1_00
);

  wire and_1_out, and_2_out, and_4_out, and_5_out, and_6_out, and_7_out, and_8_out, not_1_out, not_2_out,
       not_3_out, not_4_out, not_5_out, not_6_out, not_7_out, not_8_out;

  not not_1 (not_1_out, A);
  not not_2 (not_2_out, C);
  not not_3 (not_3_out, B);
  not not_4 (not_4_out, D);
  not not_5 (not_5_out, E);
  not not_6 (not_6_out, F);
  not not_7 (not_7_out, G);
  not not_8 (not_8_out, H);
  and and_1 (and_1_out, A, not_3_out, not_4_out, not_5_out, F, not_7_out, not_8_out);
  and and_2 (and_2_out, not_1_out, B, C, not_4_out, not_5_out, F, not_7_out, not_8_out);
  and and_3 (Refri, A, not_3_out, not_4_out, not_5_out, not_6_out, G, not_8_out);
  and and_4 (and_4_out, not_1_out, C, not_4_out, not_5_out, not_6_out, not_7_out, H);
  and and_5 (and_5_out, not_1_out, B, not_4_out, not_5_out, not_6_out, not_7_out, H);
  and and_6 (and_6_out, A, not_3_out, not_4_out, not_5_out, not_6_out, not_7_out, H);
  and and_7 (and_7_out, A, not_3_out, C, not_4_out, not_5_out, not_6_out, G, not_8_out);
  and and_8 (and_8_out, A, not_3_out, not_2_out, not_4_out, not_5_out, F, not_7_out, not_8_out);
  and and_9 (Troco_1_00, A, not_3_out, C, not_4_out, not_5_out, F, not_7_out, not_8_out);
  or or_1 (Agua, and_1_out, and_2_out);
  or or_2 (Devolve, and_4_out, and_5_out, and_6_out);
  or or_3 (Troco_0_5, and_7_out, and_8_out);

  // Notes on the sheet:
  //   A
  //   C
  //   B
  //   E
  //   D
  //   F
  //   G
  //   H
endmodule
